# Fritzing sketch VS_garden (saved by Fritzing 0.9.2b)
circuit board: 8.46667cm x 5.64444cm
breadboards: 1

parts:
  U1 = SHT1x Humdity Sensor [package=sht1x]
  U2 = SHT1x Humdity Sensor [package=sht1x]
  U3 = SHT1x Humdity Sensor [package=sht1x]
  pH_Circuit1 = pH Circuit
  Q2 = NPN-Transistor [package="TO92 [THT]"]
  R1 = Resistor [tolerance=±5% resistance=1k package=THT]
  VALVE1 = Plastic Solenoid Valve
  VALVE2 = Plastic Solenoid Valve
  VALVE3 = Plastic Solenoid Valve
  Q3 = NPN-Transistor [package="TO92 [THT]"]
  Q4 = NPN-Transistor [package="TO92 [THT]"]
  Q5 = NPN-Transistor [package="TO92 [THT]"]
  R2 = Resistor [tolerance=±5% resistance=1k package=THT]
  R3 = Resistor [tolerance=±5% resistance=1k package=THT]
  R4 = Resistor [tolerance=±5% resistance=1k package=THT]
  M1 = DC Motor
  Part2 = Arduino Uno (Rev3)
  U5 = Voltage Regulator - 5V [package="DPak [SMD]"]
  VCC2 = 4 x AAA Battery Mount
  R5 = Resistor [tolerance=±5% resistance=10k package=THT]
  R6 = Resistor [tolerance=±5% resistance=10k package=THT]
  R7 = Resistor [tolerance=±5% resistance=10k package=THT]

nets (from the breadboard view):
  GND: U1.GND, U2.GND, U3.GND, pH_Circuit1.GND, Q2.C, Q3.C, Q4.C, Q5.C, Part2.GND, U5.GND, VCC2.-
  N1: U1.DATA, Part2.D9_PWM, R6.Pin_0
  N2: U1.SCK, U2.SCK, U3.SCK, Part2.D6_PWM
  VDD: U1.VDD, U2.VDD, U3.VDD, pH_Circuit1.Vcc, Part2.5V, R5.Pin_1, R6.Pin_1, R7.Pin_1
  N3: U2.DATA, Part2.D8, R7.Pin_0
  N4: U3.DATA, Part2.D10_PWM/SS, R5.Pin_0
  N5: pH_Circuit1.TX, Part2.A4/SDA
  N6: pH_Circuit1.RX, Part2.A5/SCL
  N7: Q2.E, M1.pin_2
  N8: Q2.B, R1.Pin_1
  N9: R1.Pin_0, Part2.D2
  N10: VALVE1.no_name_yet#1, Q3.E
  N11: VALVE1.no_name_yet#2, VALVE2.no_name_yet#2, VALVE3.no_name_yet#2, Part2.VIN, U5.output_voltage
  N12: VALVE2.no_name_yet#1, Q4.E
  N13: VALVE3.no_name_yet#1, Q5.E
  N14: Q3.B, R2.Pin_1
  N15: Q4.B, R3.Pin_1
  N16: Q5.B, R4.Pin_1
  N17: R2.Pin_0, Part2.D3_PWM
  N18: R3.Pin_0, Part2.D4
  N19: R4.Pin_0, Part2.D5_PWM
  N20: U5.input_voltage, VCC2.+
